# Fritzing sketch PCB (saved by Fritzing 1.0.1rc)
circuit board: 3.5cm x 3.52047cm

parts:
  part = female pin header, 1 pin [form="♀ (female)"]
  part_2 = female pin header, 1 pin [form="♀ (female)"]
  part_3 = female pin header, 4 pins [form="♀ (female)"]
  part_4 = female pin header, 4 pins [form="♀ (female)"]
  part_5 = female pin header, 1 pin [form="♀ (female)"]
  J6 = double row female pin header, 10 pins [form="♀ (female)"]

nets:
  N1: part.pin1, J6.pin1
  N2: part_2.pin1, part_5.pin1, J6.pin10
  N3: part_3.pin1, J6.pin6
  N4: part_3.pin2, J6.pin7
  N5: part_3.pin3, J6.pin8
  N6: part_3.pin4, J6.pin9
  N7: part_4.pin1, J6.pin5
  N8: part_4.pin2, J6.pin4
  N9: part_4.pin3, J6.pin3
  N10: part_4.pin4, J6.pin2

notes:
  12
  14
  27
  15
  2
  0
  4
  STEP
  DIR
  X
  Y
  Z
  A
  5V
  GND
  EN
  26
  CNC V3 ESP-WROOM-32
